# Fritzing sketch MiriBoat (saved by Fritzing 0.9.3b)
breadboards: 1

parts:
  Componente3 = Arduino Pro Mini (5V)
  Componente4 = Bluetooth HC-05 Macho
  J1 = Basic Servo
  M1 = DC Motor
  VCC1 = Battery block 9V
  S1 = H-Bridge with L298N

nets:
  VCC: Componente3.VCC, Componente4.VCC
  N1: Componente3.RAW, VCC1.+, S1.12V
  GND: Componente3.GND, Componente4.GND, J1.gnd, VCC1.-, S1.GND
  N2: Componente3.D5, S1.IN4
  N3: Componente3.D4, S1.IN3
  N4: Componente3.D3, J1.pulse
  N5: Componente3.RXI, Componente4.TXD
  N6: J1.vcc, M1.pin_1, M1.pin_2, S1.ENA, S1.M1-02, S1.M2-01, S1.M2-02, S1.ENA-5V, S1.ENB-5V

custom parts:
  H-Bridge with L298N: h-bridge
